// Logisim project dekoder.circ as structural Verilog: 1 circuit, main circuit main
module main (
  input  [2:0] in_1
);

  wire nand_1_out, nand_2_out, not_1_out, not_2_out, or_1_out, xor_1_out, xor_2_out;

  xor xor_1 (xor_1_out, in_1[0], in_1[2]);
  not not_1 (not_1_out, in_1[1]);
  or or_1 (or_1_out, in_1[0], not_2_out, in_1[2]);
  not not_2 (not_2_out, in_1[1]);
  xor xor_2 (xor_2_out, in_1[0], in_1[1]);
  nand nand_1 (nand_1_out, xor_1_out, not_1_out);
  nand nand_2 (nand_2_out, xor_2_out, in_1[2]);
  _7_Segment_Display u_7_segment_display_1 (.a(nand_1_out), .b(nand_2_out), .c(or_1_out));  // open: g, f, e, d, dp

  // Notes on the sheet:
  //   A
  //   B
  //   C
endmodule
